# Fritzing sketch stairlights_circuit_diagram (saved by Fritzing 0.7.12b)

parts:
  Arduino1 = Arduino
  IR1 = TSOP312.., 314.. [package=THT]  # not connected
  IR2 = TSOP312.., 314.. [package=THT]  # not connected
  Part1 = Max Power IR LED Kit
  Part2 = Max Power IR LED Kit
  LED1 = RGB LED (com. cathode, rgb) [package="5 mm [THT]"]

nets:
  N1: Arduino1.GND, LED1.common_cathode
  N2: Arduino1.D7, LED1.red_anode
  N3: Arduino1.D6, LED1.green_anode
  N4: Part1.CONTROL, Part2.CONTROL
